// Logisim project Kolo 1.circ as structural Verilog: 1 circuit, main circuit main
module main (
  input  x2,
  input  x1,
  output y
);

  wire and_1_out, and_2_out;

  and and_1 (and_1_out, x1, x2);
  and and_2 (and_2_out, x1, x2);
  or or_1 (y, and_1_out, and_2_out);
endmodule
